// Logisim project Processor_8.circ as structural Verilog: 8 circuits, main circuit Latches
module Latches (
  input  D,
  input  S,
  input  E,
  input  E_2,
  input  R,
  input  D_2,
  input  E_3,
  output Q,
  output Q_2,
  output Q_bar,
  output Q_3,
  output Q_bar_2
);

  wire nand_1_out, nand_2_out, nand_3_out, nand_4_out, nand_9_out, nand_10_out, nand_12_out, not_1_out;

  not not_1 (not_1_out, D_2);
  nand nand_1 (nand_1_out, S, E);
  nand nand_2 (nand_2_out, E, R);
  nand nand_3 (nand_3_out, D_2, E_3);
  nand nand_4 (nand_4_out, E_3, not_1_out);
  nand nand_5 (Q_2, nand_1_out, Q_bar);
  nand nand_6 (Q_bar, Q_2, nand_2_out);
  nand nand_7 (Q_3, nand_3_out, Q_bar_2);
  nand nand_8 (Q_bar_2, Q_3, nand_4_out);
  nand nand_9 (nand_9_out, D, E_2);
  nand nand_10 (nand_10_out, nand_9_out, E_2);
  nand nand_11 (Q, nand_9_out, nand_12_out);
  nand nand_12 (nand_12_out, Q, nand_10_out);

  // Notes on the sheet:
  //   SR
  //   D-FlipFlop 
  //   1-Bit-Memory Cell
endmodule

module P_MEM1 (
  input  D,
  input  E,
  output Q
);

  wire nand_1_out, nand_2_out, nand_4_out;

  nand nand_1 (nand_1_out, D, E);
  nand nand_2 (nand_2_out, nand_1_out, E);
  nand nand_3 (Q, nand_1_out, nand_4_out);
  nand nand_4 (nand_4_out, Q, nand_2_out);

  // Notes on the sheet:
  //   1-Bit-Memory Cell
endmodule

module P_MEM8 (
  input  [7:0] in_1,
  input  in_2,
  output [7:0] out_3
);

  P_MEM1 p_mem1_1 (.D(in_1[0]), .E(in_2), .Q(out_3[0]));
  P_MEM1 p_mem1_2 (.D(in_1[1]), .E(in_2), .Q(out_3[1]));
  P_MEM1 p_mem1_3 (.D(in_1[2]), .E(in_2), .Q(out_3[2]));
  P_MEM1 p_mem1_4 (.D(in_1[3]), .E(in_2), .Q(out_3[3]));
  P_MEM1 p_mem1_5 (.D(in_1[4]), .E(in_2), .Q(out_3[4]));
  P_MEM1 p_mem1_6 (.D(in_1[5]), .E(in_2), .Q(out_3[5]));
  P_MEM1 p_mem1_7 (.D(in_1[6]), .E(in_2), .Q(out_3[6]));
  P_MEM1 p_mem1_8 (.D(in_1[7]), .E(in_2), .Q(out_3[7]));
endmodule

module P_ENABLE (
  input  [7:0] in_1,
  input  in_2,
  output [7:0] out_3
);

  and and_1 (out_3[0], in_1[0], in_2);
  and and_2 (out_3[1], in_1[1], in_2);
  and and_3 (out_3[2], in_1[2], in_2);
  and and_4 (out_3[3], in_1[3], in_2);
  and and_5 (out_3[4], in_1[4], in_2);
  and and_6 (out_3[5], in_1[5], in_2);
  and and_7 (out_3[6], in_1[6], in_2);
  and and_8 (out_3[7], in_1[7], in_2);
endmodule

module P_REG_8 (
  input  [7:0] in_1,
  input  E1,
  input  E2,
  output [7:0] out_4
);

  wire [7:0] p_mem8_1_out_3;

  P_MEM8 p_mem8_1 (.in_1(in_1), .out_3(p_mem8_1_out_3), .in_2(E1));
  P_ENABLE p_enable_1 (.in_1(p_mem8_1_out_3), .out_3(out_4), .in_2(E2));
endmodule

module P_DECODER_4x16 (
  input  [3:0] in_1,
  output out_2,
  output out_3,
  output out_4,
  output out_5,
  output out_6,
  output out_7,
  output out_8,
  output out_9,
  output out_10,
  output out_11,
  output out_12,
  output out_13,
  output out_14,
  output out_15,
  output out_16,
  output out_17
);

  wire not_1_out, not_2_out, not_3_out, not_4_out;

  not not_1 (not_1_out, in_1[0]);
  not not_2 (not_2_out, in_1[1]);
  not not_3 (not_3_out, in_1[2]);
  not not_4 (not_4_out, in_1[3]);
  and and_1 (out_2, not_4_out, not_3_out, not_2_out, not_1_out);
  and and_2 (out_3, not_4_out, not_3_out, not_2_out, in_1[0]);
  and and_3 (out_4, not_4_out, not_3_out, in_1[1], not_1_out);
  and and_4 (out_5, not_4_out, not_3_out, in_1[1], in_1[0]);
  and and_5 (out_6, not_4_out, in_1[2], not_2_out, not_1_out);
  and and_6 (out_7, not_4_out, in_1[2], not_2_out, in_1[0]);
  and and_7 (out_8, not_4_out, in_1[2], in_1[1], not_1_out);
  and and_8 (out_9, not_4_out, in_1[2], in_1[1], in_1[0]);
  and and_9 (out_10, in_1[3], not_3_out, not_2_out, not_1_out);
  and and_10 (out_11, in_1[3], not_3_out, not_2_out, in_1[0]);
  and and_11 (out_12, in_1[3], not_3_out, in_1[1], not_1_out);
  and and_12 (out_13, in_1[3], not_3_out, in_1[1], in_1[0]);
  and and_13 (out_14, in_1[3], in_1[2], not_2_out, not_1_out);
  and and_14 (out_15, in_1[3], in_1[2], not_2_out, in_1[0]);
  and and_15 (out_16, in_1[3], in_1[2], in_1[1], not_1_out);
  and and_16 (out_17, in_1[3], in_1[2], in_1[1], in_1[0]);
endmodule

module P_DECODER_3x8 (
  input  C,
  input  B,
  input  A,
  output [7:0] O
);

  wire not_1_out, not_2_out, not_3_out;

  not not_1 (not_1_out, A);
  not not_2 (not_2_out, B);
  not not_3 (not_3_out, C);
  and and_1 (O[0], not_1_out, not_2_out, not_3_out);
  and and_2 (O[1], not_1_out, not_2_out, C);
  and and_3 (O[2], not_1_out, B, not_3_out);
  and and_4 (O[3], not_1_out, B, C);
  and and_5 (O[4], A, not_2_out, not_3_out);
  and and_6 (O[5], A, not_2_out, C);
  and and_7 (O[6], A, B, not_3_out);
  and and_8 (O[7], A, B, C);
endmodule

module T_RAM (
  input  [7:0] in_1,
  input  [3:0] in_2,
  output [7:0] out_3,
  output [7:0] out_4,
  output [7:0] out_5
);

  wire p_decoder_4x16_1_out_2, p_decoder_4x16_1_out_3, p_decoder_4x16_1_out_4, p_decoder_4x16_1_out_5,
       p_decoder_4x16_1_out_6, p_decoder_4x16_1_out_7, p_decoder_4x16_1_out_8, p_decoder_4x16_1_out_9,
       p_decoder_4x16_1_out_10, p_decoder_4x16_1_out_11, p_decoder_4x16_1_out_12, p_decoder_4x16_1_out_13,
       p_decoder_4x16_1_out_14, p_decoder_4x16_1_out_15, p_decoder_4x16_1_out_16, p_decoder_4x16_1_out_17;

  P_DECODER_4x16 p_decoder_4x16_1 (
    .in_1(in_2), .out_2(p_decoder_4x16_1_out_2), .out_3(p_decoder_4x16_1_out_3),
    .out_4(p_decoder_4x16_1_out_4), .out_5(p_decoder_4x16_1_out_5), .out_6(p_decoder_4x16_1_out_6),
    .out_7(p_decoder_4x16_1_out_7), .out_8(p_decoder_4x16_1_out_8), .out_9(p_decoder_4x16_1_out_9),
    .out_10(p_decoder_4x16_1_out_10), .out_11(p_decoder_4x16_1_out_11), .out_12(p_decoder_4x16_1_out_12),
    .out_13(p_decoder_4x16_1_out_13), .out_14(p_decoder_4x16_1_out_14), .out_15(p_decoder_4x16_1_out_15),
    .out_16(p_decoder_4x16_1_out_16), .out_17(p_decoder_4x16_1_out_17));
  P_MEM8 p_mem8_1 (.in_1(in_1), .out_3(out_5), .in_2(p_decoder_4x16_1_out_2));
  P_MEM8 p_mem8_2 (.in_1(in_1), .out_3(out_4), .in_2(p_decoder_4x16_1_out_3));
  P_MEM8 p_mem8_3 (.in_1(in_1), .out_3(out_3), .in_2(p_decoder_4x16_1_out_4));
  P_MEM8 p_mem8_4 (.in_1(in_1), .in_2(p_decoder_4x16_1_out_5));  // open: out_3
  P_MEM8 p_mem8_5 (.in_1(in_1), .in_2(p_decoder_4x16_1_out_6));  // open: out_3
  P_MEM8 p_mem8_6 (.in_1(in_1), .in_2(p_decoder_4x16_1_out_7));  // open: out_3
  P_MEM8 p_mem8_7 (.in_2(p_decoder_4x16_1_out_8));  // open: in_1, out_3
  P_MEM8 p_mem8_8 (.in_2(p_decoder_4x16_1_out_9));  // open: in_1, out_3
  P_MEM8 p_mem8_9 (.in_2(p_decoder_4x16_1_out_10));  // open: in_1, out_3
  P_MEM8 p_mem8_10 (.in_2(p_decoder_4x16_1_out_11));  // open: in_1, out_3
  P_MEM8 p_mem8_11 (.in_2(p_decoder_4x16_1_out_12));  // open: in_1, out_3
  P_MEM8 p_mem8_12 (.in_2(p_decoder_4x16_1_out_13));  // open: in_1, out_3
  P_MEM8 p_mem8_13 (.in_2(p_decoder_4x16_1_out_14));  // open: in_1, out_3
  P_MEM8 p_mem8_14 (.in_2(p_decoder_4x16_1_out_15));  // open: in_1, out_3
  P_MEM8 p_mem8_15 (.in_2(p_decoder_4x16_1_out_16));  // open: in_1, out_3
  P_MEM8 p_mem8_16 (.in_2(p_decoder_4x16_1_out_17));  // open: in_1, out_3
  P_MEM8 p_mem8_17 ();  // open: in_1, out_3, in_2
  P_MEM8 p_mem8_18 ();  // open: in_1, out_3, in_2
  P_MEM8 p_mem8_19 ();  // open: in_1, out_3, in_2
  P_MEM8 p_mem8_20 ();  // open: in_1, out_3, in_2
  P_MEM8 p_mem8_21 ();  // open: in_1, out_3, in_2
  P_MEM8 p_mem8_22 ();  // open: in_1, out_3, in_2
  P_MEM8 p_mem8_23 ();  // open: in_1, out_3, in_2
  P_MEM8 p_mem8_24 ();  // open: in_1, out_3, in_2
  P_MEM8 p_mem8_25 ();  // open: in_1, out_3, in_2
  P_MEM8 p_mem8_26 ();  // open: in_1, out_3, in_2
  P_MEM8 p_mem8_27 ();  // open: in_1, out_3, in_2
  P_MEM8 p_mem8_28 ();  // open: in_1, out_3, in_2
  P_MEM8 p_mem8_29 ();  // open: in_1, out_3, in_2
  P_MEM8 p_mem8_30 ();  // open: in_1, out_3, in_2
  P_MEM8 p_mem8_31 ();  // open: in_1, out_3, in_2
  P_MEM8 p_mem8_32 ();  // open: in_1, out_3, in_2
  P_MEM8 p_mem8_33 ();  // open: in_1, out_3, in_2
  P_MEM8 p_mem8_34 ();  // open: in_1, out_3, in_2
  P_MEM8 p_mem8_35 ();  // open: in_1, out_3, in_2
  P_MEM8 p_mem8_36 ();  // open: in_1, out_3, in_2
endmodule
